# Fritzing sketch ramylizer_with_lcd (saved by Fritzing 0.9.3b)
breadboards: 1

parts:
  Part1 = Gas Sensor Breakout Board
  PART1 = SFE_COM-11442 [part_number=COM-11647]
  R1 = Resistor [tolerance=±5% resistance=4.7k package=THT]
  Part2 = Arduino Uno (Rev3)

nets:
  N1: Part1.A1, Part1.H1, PART1.connector3, Part2.5V
  N2: Part1.B1, R1.Pin_1, Part2.A0
  GND: Part1.GND, PART1.connector2, R1.Pin_0, Part2.GND
  N3: PART1.connector9, Part2.D8
